// Logisim project CPU.circ as structural Verilog: 10 circuits, main circuit ◇多周期MIPS(微程序)
module \单周期MIPS_硬布线  (
);

  wire and_1_out, and_2_out, CLK, mips_alu_1_equal, not_1_out, or_1_out, RST, \单周期硬布线控制器_1_alusrc ,
       \单周期硬布线控制器_1_beq , \单周期硬布线控制器_1_bne , \单周期硬布线控制器_1_halt , \单周期硬布线控制器_1_memtoreg ,
       \单周期硬布线控制器_1_memwrite , \单周期硬布线控制器_1_regdst , \单周期硬布线控制器_1_regwrite ;
  wire [3:0] \单周期硬布线控制器_1_alu_op ;
  wire [4:0] multiplexer_3_out;
  wire [9:0] mips_alu_1_result_2;
  wire [15:0] \总周期数 ;
  wire [31:0] adder_1_out, adder_2_out, bit_extender_1_out, mips_alu_1_result, mips_regifile_1_r1,
       mips_regifile_1_r2, multiplexer_1_out, multiplexer_2_out, multiplexer_4_out, multiplexer_5_out, PC_q,
       ram_1_data, rom_1_data, shifter_1_out;

  Button \u_总复位  (.out(RST));
  Multiplexer #(.width(32), .enable("false")) multiplexer_1 (
    .in0(adder_1_out), .in1(adder_2_out), .out(multiplexer_1_out), .sel(or_1_out));
  not not_1 (not_1_out, \单周期硬布线控制器_1_halt );
  Register #(.width(32)) PC (.D(multiplexer_1_out), .Q(PC_q), .clk(CLK), .clr(RST));  // open: en
  Multiplexer #(.width(32), .enable("false")) multiplexer_2 (
    .in0(32'h4), .in1({32{1'b0}}), .out(multiplexer_2_out), .sel(\单周期硬布线控制器_1_halt ));
  Clock clock_1 (.out(CLK));
  Counter #(.width(16), .max('hffff)) counter_1 (
    .count(not_1_out), .Q(\总周期数 ), .clk(CLK), .clr(RST));  // open: load, D, carry
  or or_1 (or_1_out, and_1_out, and_2_out);
  Adder #(.width(32)) adder_1 (.a(PC_q), .b(multiplexer_2_out), .out(adder_1_out));  // open: cin, cout
  and and_1 (and_1_out, mips_alu_1_equal, \单周期硬布线控制器_1_beq );
  and and_2 (and_2_out, \单周期硬布线控制器_1_bne , ~mips_alu_1_equal);  // AND_Gate
  ROM #(.addrWidth(10), .dataWidth(32)) rom_1 (.addr(PC_q[11:2]), .data(rom_1_data));  // open: sel
  assign bit_extender_1_out = {{16{rom_1_data[15]}}, rom_1_data[15:0]};  // Bit_Extender bit_extender_1
  // Probe on \总周期数 
  \单周期硬布线控制器  \u_单周期硬布线控制器_1  (
    .Func(rom_1_data[5:0]), .RegWrite(\单周期硬布线控制器_1_regwrite ), .MemToReg(\单周期硬布线控制器_1_memtoreg ),
    .MemWrite(\单周期硬布线控制器_1_memwrite ), .Beq(\单周期硬布线控制器_1_beq ), .Bne(\单周期硬布线控制器_1_bne ),
    .RegDst(\单周期硬布线控制器_1_regdst ), .AluSrc(\单周期硬布线控制器_1_alusrc ), .ALU_OP(\单周期硬布线控制器_1_alu_op ),
    .OP(rom_1_data[31:26]), .Halt(\单周期硬布线控制器_1_halt ));
  Multiplexer #(.width(5), .enable("false")) multiplexer_3 (
    .in0(rom_1_data[20:16]), .in1(rom_1_data[15:11]), .out(multiplexer_3_out), .sel(\单周期硬布线控制器_1_regdst ));
  MIPS_Regifile mips_regifile_1 (
    .Din(multiplexer_5_out), .Clk(CLK), .R1(mips_regifile_1_r1), .R2(mips_regifile_1_r2),
    .WE(\单周期硬布线控制器_1_regwrite ), .W_num(multiplexer_3_out), .R1_num(rom_1_data[25:21]),
    .R2_num(rom_1_data[20:16]));
  Multiplexer #(.width(32), .enable("false")) multiplexer_4 (
    .in0(mips_regifile_1_r2), .in1(bit_extender_1_out), .out(multiplexer_4_out), .sel(\单周期硬布线控制器_1_alusrc ));
  Shifter #(.width(32)) shifter_1 (.in(bit_extender_1_out), .\dist (5'b00010), .out(shifter_1_out));
  Adder #(.width(32)) adder_2 (.a(shifter_1_out), .b(adder_1_out), .out(adder_2_out));  // open: cin, cout
  MIPS_ALU mips_alu_1 (
    .X(mips_regifile_1_r1), .Y(multiplexer_4_out), .AluOP(\单周期硬布线控制器_1_alu_op ), .Equal(mips_alu_1_equal),
    .Result({mips_alu_1_result[31:12], mips_alu_1_result_2, mips_alu_1_result[1:0]}));  // open: Result_2
  RAM #(.addrWidth(10), .dataWidth(32), .bus("separate")) ram_1 (
    .addr(mips_alu_1_result_2), .din(mips_regifile_1_r2), .data(ram_1_data), .str(\单周期硬布线控制器_1_memwrite ),
    .clk(CLK), .clr(RST));  // open: sel, ld
  Multiplexer #(.width(32), .enable("false")) multiplexer_5 (
    .in0({mips_alu_1_result[31:12], mips_alu_1_result_2, mips_alu_1_result[1:0]}), .in1(ram_1_data),
    .out(multiplexer_5_out), .sel(\单周期硬布线控制器_1_memtoreg ));

  // Notes on the sheet:
  //   指令存储器
  //   Ctrl+K  Command+K触发时钟连续仿真，程序运行结束后可停机，查看数据存储器中80单元的排序情况是有符号降序
  //   contents of rom_1 (hex, n*v repeats v):
  //   2010ffff 20110000 ae300200 22100001 22310004 ae300200 22100001 22310004 ae300200 22100001 22310004
  //   ae300200 22100001 22310004 ae300200 22100001 22310004 ae300200 22100001 22310004 ae300200 22100001
  //   22310004 ae300200 8020 2011001c 8e130200 8e340200 274402a 11000002 ae330200 ae140200 2231fffc
  //   1611fff8 22100004 2011001c 1611fff5 2002000a c
  //   Halt
  //   Op
  //   Func
  //   MemToReg
  //   MemWrite
  //   Beq
  //   Bne
  //   AluOP
  //   AluSrcB
  //   RegWrite
  //   RegDst
endmodule

// 单周期硬布线控制器
module \单周期硬布线控制器  (
  input  [5:0] OP,
  input  [5:0] Func,
  output [3:0] ALU_OP,
  output RegDst,
  output RegWrite,
  output MemToReg,
  output MemWrite,
  output AluSrc,
  output Beq,
  output Bne,
  output Halt
);

  wire ADD, ADDI, and_3_out, comparator_6_eq, comparator_9_eq, comparator_10_eq, comparator_11_eq, or_2_out,
       SLT;

  Comparator #(.width(6)) comparator_1 (.a(OP), .b(6'b100011), .eq(MemToReg));  // open: gt, lt
  Comparator #(.width(6)) comparator_2 (.a(OP), .b(6'b101011), .eq(MemWrite));  // open: gt, lt
  Comparator #(.width(6)) comparator_3 (.a(OP), .b(6'b000100), .eq(Beq));  // open: gt, lt
  Comparator #(.width(6)) comparator_4 (.a(OP), .b(6'b000101), .eq(Bne));  // open: gt, lt
  Comparator #(.width(6)) comparator_5 (.a(OP), .b(6'b001000), .eq(ADDI));  // open: gt, lt
  Comparator #(.width(6)) comparator_6 (.a(OP), .b({6{1'b0}}), .eq(comparator_6_eq));  // open: gt, lt
  or or_1 (RegWrite, RegDst, ADDI, MemToReg);
  or or_2 (or_2_out, ADD, SLT);
  Comparator #(.width(6)) comparator_7 (.a(Func), .b(6'b100000), .eq(ADD));  // open: gt, lt
  Comparator #(.width(6)) comparator_8 (.a(Func), .b(6'b101010), .eq(SLT));  // open: gt, lt
  Comparator #(.width(6)) comparator_9 (.a(Func), .b(6'b001100), .eq(comparator_9_eq));  // open: gt, lt
  and and_1 (RegDst, comparator_6_eq, or_2_out);
  and and_2 (Halt, comparator_9_eq, comparator_6_eq);
  nor nor_1 (AluSrc, RegDst, Beq, Bne);
  Comparator #(.width(6)) comparator_10 (.a(OP), .b({6{1'b0}}), .eq(comparator_10_eq));  // open: gt, lt
  and and_3 (and_3_out, comparator_10_eq, comparator_11_eq);
  Comparator #(.width(6)) comparator_11 (.a(6'b101010), .b(Func), .eq(comparator_11_eq));  // open: gt, lt
  Multiplexer #(.width(4), .enable("false")) multiplexer_1 (
    .in0(4'b0101), .in1(4'b1011), .out(ALU_OP), .sel(and_3_out));

  // Other names for the same wires on the sheet: LW = MemToReg; R_TYPE = RegDst; SW = MemWrite; SysCall = Halt

  // Notes on the sheet:
  //   指令译码信号
  //   指令译码逻辑
  //   给出简单的逻辑实现对应指令译码信号，LW、SW、BEQ、BNE、ADDI、ADD、SLT、SYSCALL、R_TYPE。
  //   ALU控制器逻辑
  //   注意R_TYPE表示R型运算指令，SYSCALL是特殊的R型指令，不属于这个类别
  //   根据指令译码信号实现控制器输出控制信号的逻辑
  //   给出简单的逻辑实现ALU_OP与OP、Func之间的对应关系
  //   控制信号
endmodule

module \多周期MIPS_微程序  (
);

  wire and_1_out, and_2_out, CLK, comparator_1_eq, mips_alu_1_equal, not_1_out, or_1_out, RST,
       \多周期微程序控制器_1_alusrca , \多周期微程序控制器_1_beq , \多周期微程序控制器_1_bne , \多周期微程序控制器_1_iord ,
       \多周期微程序控制器_1_irwrite , \多周期微程序控制器_1_memread , \多周期微程序控制器_1_memtoreg , \多周期微程序控制器_1_memwrite ,
       \多周期微程序控制器_1_pcsrc , \多周期微程序控制器_1_pcwrite , \多周期微程序控制器_1_regdst , \多周期微程序控制器_1_regwrite ;
  wire [1:0] \多周期微程序控制器_1_alusrcb ;
  wire [3:0] \多周期微程序控制器_1_alu_op , \多周期微程序控制器_1_当前微指令地址 ;
  wire [4:0] IR_q, IR_q_2, IR_q_5, IR_q_6, multiplexer_2_out;
  wire [5:0] IR_q_3, IR_q_4;
  wire [15:0] \总周期数 ;
  wire [31:0] A_q, B_q, bit_extender_1_out, C_q, DR_q, mips_alu_1_result, mips_regifile_1_r1,
       mips_regifile_1_r2, multiplexer_1_out, multiplexer_3_out, multiplexer_4_out, multiplexer_5_out,
       multiplexer_6_out, PC_q, ram_1_data, shifter_1_out;

  Button \u_总复位  (.out(RST));
  Comparator #(.width(32)) comparator_1 (
    .a(32'hc), .b({IR_q_3, IR_q_2, IR_q, IR_q_6, IR_q_5, IR_q_4}), .eq(comparator_1_eq));  // open: gt, lt
  not not_1 (not_1_out, comparator_1_eq);
  Register #(.width(32)) PC (.D(multiplexer_6_out), .en(or_1_out), .Q(PC_q), .clk(CLK), .clr(RST));
  Multiplexer #(.width(32), .enable("false")) multiplexer_1 (
    .in0(PC_q), .in1(C_q), .out(multiplexer_1_out), .sel(\多周期微程序控制器_1_iord ));
  Clock clock_1 (.out(CLK));
  Counter #(.width(16), .max('hffff)) counter_1 (
    .count(not_1_out), .Q(\总周期数 ), .clk(CLK), .clr(RST));  // open: load, D, carry
  or or_1 (or_1_out, \多周期微程序控制器_1_pcwrite , and_1_out, and_2_out);
  and and_1 (and_1_out, \多周期微程序控制器_1_beq , mips_alu_1_equal);
  and and_2 (and_2_out, \多周期微程序控制器_1_bne , ~mips_alu_1_equal);  // AND_Gate
  RAM #(.addrWidth(10), .dataWidth(32), .bus("separate")) ram_1 (
    .addr(multiplexer_1_out[11:2]), .din(B_q), .data(ram_1_data), .str(\多周期微程序控制器_1_memwrite ), .clk(CLK),
    .ld(\多周期微程序控制器_1_memread ));  // open: sel, clr
  // Probe on \多周期微程序控制器_1_当前微指令地址 
  Register #(.width(32)) IR (
    .D(ram_1_data), .en(\多周期微程序控制器_1_irwrite ), .Q({IR_q_3, IR_q_2, IR_q, IR_q_6, IR_q_5, IR_q_4}),
    .clk(CLK), .clr(RST));
  Register #(.width(32)) DR (.D(ram_1_data), .Q(DR_q), .clk(CLK), .clr(RST));  // open: en
  // Probe on \总周期数 
  \多周期微程序控制器  \u_多周期微程序控制器_1  (
    .PcWrite(\多周期微程序控制器_1_pcwrite ), .Beq(\多周期微程序控制器_1_beq ), .PCsrc(\多周期微程序控制器_1_pcsrc ),
    .AluSrcB(\多周期微程序控制器_1_alusrcb ), .AluSrcA(\多周期微程序控制器_1_alusrca ), .RegWrite(\多周期微程序控制器_1_regwrite ),
    .MemToReg(\多周期微程序控制器_1_memtoreg ), .RegDst(\多周期微程序控制器_1_regdst ), .IorD(\多周期微程序控制器_1_iord ),
    .MemWrite(\多周期微程序控制器_1_memwrite ), .MemRead(\多周期微程序控制器_1_memread ), .IrWrite(\多周期微程序控制器_1_irwrite ),
    .Bne(\多周期微程序控制器_1_bne ), .CLK(CLK), .\当前微指令地址 (\多周期微程序控制器_1_当前微指令地址 ), .RST(RST), .OP(IR_q_3),
    .ALU_OP(\多周期微程序控制器_1_alu_op ), .Func(IR_q_4));
  Multiplexer #(.width(5), .enable("false")) multiplexer_2 (
    .in0(IR_q), .in1(IR_q_6), .out(multiplexer_2_out), .sel(\多周期微程序控制器_1_regdst ));
  assign bit_extender_1_out = {{16{IR_q_6[4]}}, {IR_q_6, IR_q_5, IR_q_4}};  // Bit_Extender bit_extender_1
  Multiplexer #(.width(32), .enable("false")) multiplexer_3 (
    .in0(C_q), .in1(DR_q), .out(multiplexer_3_out), .sel(\多周期微程序控制器_1_memtoreg ));
  Shifter #(.width(32)) shifter_1 (.in(bit_extender_1_out), .\dist (5'b00010), .out(shifter_1_out));
  MIPS_Regifile mips_regifile_1 (
    .Din(multiplexer_3_out), .Clk(CLK), .R1(mips_regifile_1_r1), .R2(mips_regifile_1_r2),
    .WE(\多周期微程序控制器_1_regwrite ), .W_num(multiplexer_2_out), .R1_num(IR_q_2), .R2_num(IR_q));
  Multiplexer #(.width(32), .enable("false")) multiplexer_4 (
    .in0(PC_q), .in1(A_q), .out(multiplexer_4_out), .sel(\多周期微程序控制器_1_alusrca ));
  Register #(.width(32)) A (.D(mips_regifile_1_r1), .Q(A_q), .clk(CLK), .clr(RST));  // open: en
  Register #(.width(32)) B (.D(mips_regifile_1_r2), .Q(B_q), .clk(CLK), .clr(RST));  // open: en
  Multiplexer #(.select(2), .width(32), .enable("false")) multiplexer_5 (
    .in0(B_q), .in1(32'h4), .in2(bit_extender_1_out), .in3(shifter_1_out), .out(multiplexer_5_out),
    .sel(\多周期微程序控制器_1_alusrcb ));
  MIPS_ALU mips_alu_1 (
    .X(multiplexer_4_out), .Y(multiplexer_5_out), .AluOP(\多周期微程序控制器_1_alu_op ), .Equal(mips_alu_1_equal),
    .Result(mips_alu_1_result));  // open: Result_2
  Register #(.width(32)) C (.D(mips_alu_1_result), .Q(C_q), .clk(CLK), .clr(RST));  // open: en
  Multiplexer #(.width(32), .enable("false")) multiplexer_6 (
    .in0(mips_alu_1_result), .in1(C_q), .out(multiplexer_6_out), .sel(\多周期微程序控制器_1_pcsrc ));

  // Notes on the sheet:
  //   存储器
  //   Ctrl+K  Command+K触发时钟连续仿真，程序运行结束后可停机，查看数据存储器中80单元的排序情况是有符号降序
  //   MemWrite
  //   MemRead
  //   IorD
  //   IRWrite
  //   OP
  //   Func
  //   RegDst
  //   PcWrite
  //   Beq
  //   Bne
  //   PcSrc
  //   AluOP
  //   AluSrcB
  //   AluSrcA
  //   RegWrite
  //   MemToReg
endmodule

// 微程序控制器
module \多周期微程序控制器  (
  input  [5:0] OP,
  input  [5:0] Func,
  input  CLK,
  input  RST,
  output [3:0] ALU_OP,
  output Bne,
  output Beq,
  output MemRead,
  output MemWrite,
  output RegWrite,
  output PcWrite,
  output IrWrite,
  output RegDst,
  output MemToReg,
  output [3:0] \当前微指令地址 ,
  output [1:0] AluSrcB,
  output AluSrcA,
  output PCsrc,
  output IorD
);

  wire ADD, ADDI, BEQ_t, BNE_t, comparator_6_eq, comparator_9_eq, LW, or_1_out, P, R_TYPE, SLT, SW, SysCall;
  wire [1:0] ALU_Control;
  wire [3:0] and_3_out, and_4_out, multiplexer_1_out, or_2_out, rom_1_data, \微程序地址转移逻辑_1_s0 ;
  wire [3:3] comparator_10_eq, comparator_11_eq;

  Comparator #(.width(6)) comparator_1 (.a(OP), .b(6'b100011), .eq(LW));  // open: gt, lt
  Comparator #(.width(6)) comparator_2 (.a(OP), .b(6'b101011), .eq(SW));  // open: gt, lt
  Comparator #(.width(6)) comparator_3 (.a(OP), .b(6'b000100), .eq(BEQ_t));  // open: gt, lt
  Comparator #(.width(6)) comparator_4 (.a(OP), .b(6'b000101), .eq(BNE_t));  // open: gt, lt
  Comparator #(.width(6)) comparator_5 (.a(OP), .b(6'b001000), .eq(ADDI));  // open: gt, lt
  Comparator #(.width(6)) comparator_6 (.a(OP), .b({6{1'b0}}), .eq(comparator_6_eq));  // open: gt, lt
  \微程序地址转移逻辑  \u_微程序地址转移逻辑_1  (
    .R_Type(R_TYPE), .S3(\微程序地址转移逻辑_1_s0 [3]), .ADDI(ADDI), .LW(LW), .S1(\微程序地址转移逻辑_1_s0 [1]), .SW(SW),
    .S0(\微程序地址转移逻辑_1_s0 [0]), .BEQ(BEQ_t), .BNE(BNE_t), .SYSCALL(SysCall), .S2(\微程序地址转移逻辑_1_s0 [2]));
  or or_1 (or_1_out, ADD, SLT);
  Comparator #(.width(6)) comparator_7 (.a(Func), .b(6'b100000), .eq(ADD));  // open: gt, lt
  Comparator #(.width(6)) comparator_8 (.a(Func), .b(6'b101010), .eq(SLT));  // open: gt, lt
  Comparator #(.width(6)) comparator_9 (.a(Func), .b(6'b001100), .eq(comparator_9_eq));  // open: gt, lt
  Register #(.width(4)) register_1 (.D(multiplexer_1_out), .Q(\当前微指令地址 ), .clk(CLK), .clr(RST));  // open: en
  Multiplexer #(.width(4), .enable("false")) multiplexer_1 (
    .in0(rom_1_data), .in1(\微程序地址转移逻辑_1_s0 ), .out(multiplexer_1_out), .sel(P));
  and and_1 (R_TYPE, comparator_6_eq, or_1_out);
  and and_2 (SysCall, comparator_6_eq, comparator_9_eq);
  ROM #(.addrWidth(4), .dataWidth(21)) rom_1 (
    .addr(\当前微指令地址 ),
    .data({IorD, PCsrc, AluSrcA, AluSrcB, MemToReg, RegDst, IrWrite, PcWrite, RegWrite, MemWrite, MemRead, Beq, Bne, ALU_Control, P, rom_1_data}));  // open: sel
  Comparator #(.width(6)) comparator_10 (.a(Func), .b(6'b101010), .eq(comparator_10_eq[3]));  // open: gt, lt
  Comparator #(.width(6)) comparator_11 (.a(Func), .b(6'b100000), .eq(comparator_11_eq[3]));  // open: gt, lt
  assign and_3_out = {4{comparator_10_eq[3]}} & 4'b1011;  // AND_Gate and_3, 4 bits wide
  assign and_4_out = {4{comparator_11_eq[3]}} & 4'b0101;  // AND_Gate and_4, 4 bits wide
  assign or_2_out = and_3_out | and_4_out;  // OR_Gate or_2, 4 bits wide
  Multiplexer #(.select(2), .width(4), .enable("false")) multiplexer_2 (
    .in0(4'b0101), .in1(4'b0110), .in2(or_2_out), .in3(4'b0101), .out(ALU_OP), .sel(ALU_Control));

  // Notes on the sheet:
  //   指令译码信号
  //   根据指令进行微程序地址转移
  //   指令译码逻辑
  //   给出简单的逻辑实现对应指令译码信号，LW、SW、BEQ、BNE、ADDI、ADD、SLT、SYSCALL、R_TYPE。
  //   下址字段
  //   微程序入口地址
  //   判断逻辑
  //   μAR
  //   微程序控制器
  //   contents of rom_1 (hex, n*v repeats v):
  //   13201 30010 60003 130204 38800 60006 130400 40048 34800 c0100 c0080 6000c 30800 d
  //   微命令
  //   ALU控制器逻辑
  //   根据ALU_Control的值决定运算器运算选择控制信号ALU_OP的值
  //   注意R_TYPE表示R型运算指令，SYSCALL是特殊的R型指令，不属于这个类别
  //   微指令
  //   下址字段
  //   判断逻辑
  //   ALU_Control= 00 运算器做加法
  //   ALU_Control= 01 运算器做减法
  //   ALU_Control= 10 运算方式由Func决定 
endmodule

// 地址转移逻辑
module \微程序地址转移逻辑  (
  input  R_Type,
  input  ADDI,
  input  LW,
  input  SW,
  input  BEQ,
  input  BNE,
  input  SYSCALL,
  output S3,
  output S2,
  output S1,
  output S0
);

  wire not_1_out, not_2_out, not_3_out, not_4_out, not_5_out, not_6_out, not_7_out, not_8_out, not_9_out,
       not_10_out, not_11_out, not_12_out;

  not not_1 (not_1_out, R_Type);
  not not_2 (not_2_out, LW);
  not not_3 (not_3_out, SW);
  not not_4 (not_4_out, ADDI);
  not not_5 (not_5_out, LW);
  not not_6 (not_6_out, BEQ);
  not not_7 (not_7_out, BNE);
  not not_8 (not_8_out, SW);
  not not_9 (not_9_out, BEQ);
  not not_10 (not_10_out, SYSCALL);
  not not_11 (not_11_out, LW);
  not not_12 (not_12_out, BNE);
  and and_1 (S3, not_1_out, not_2_out, not_3_out);
  and and_2 (S2, not_4_out, not_5_out, not_6_out, not_7_out);
  and and_3 (S1, not_8_out, not_9_out, not_10_out);
  and and_4 (S0, not_11_out, not_12_out);

  // Notes on the sheet:
  //   选择项目菜单中的分析电路----输入表达式自动生成
endmodule

module \多周期MIPS_硬布线  (
);

  wire and_1_out, and_2_out, CLK, comparator_1_eq, mips_alu_1_equal, not_1_out, or_1_out, RST,
       \多周期硬布线控制器_1_alusrca , \多周期硬布线控制器_1_beq , \多周期硬布线控制器_1_bne , \多周期硬布线控制器_1_iord ,
       \多周期硬布线控制器_1_irwrite , \多周期硬布线控制器_1_memread , \多周期硬布线控制器_1_memtoreg , \多周期硬布线控制器_1_memwrite ,
       \多周期硬布线控制器_1_pcsrc , \多周期硬布线控制器_1_pcwrite , \多周期硬布线控制器_1_regdst , \多周期硬布线控制器_1_regwrite ;
  wire [1:0] \多周期硬布线控制器_1_alusrcb ;
  wire [3:0] \多周期硬布线控制器_1_alu_op , \多周期硬布线控制器_1_当前状态 ;
  wire [4:0] multiplexer_2_out;
  wire [15:0] \总周期数 ;
  wire [31:0] A_q, B_q, bit_extender_1_out, C_q, DR_q, IR_q, mips_alu_1_result, mips_regifile_1_r1,
       mips_regifile_1_r2, multiplexer_1_out, multiplexer_3_out, multiplexer_4_out, multiplexer_5_out,
       multiplexer_6_out, PC_q, ram_1_data, shifter_1_out;

  Button \u_总复位  (.out(RST));
  Register #(.width(32)) PC (.D(multiplexer_6_out), .en(or_1_out), .Q(PC_q), .clk(CLK), .clr(RST));
  Multiplexer #(.width(32), .enable("false")) multiplexer_1 (
    .in0(PC_q), .in1(C_q), .out(multiplexer_1_out), .sel(\多周期硬布线控制器_1_iord ));
  Clock clock_1 (.out(CLK));
  Counter #(.width(16), .max('hffff)) counter_1 (
    .count(not_1_out), .Q(\总周期数 ), .clk(CLK), .clr(RST));  // open: load, D, carry
  not not_1 (not_1_out, comparator_1_eq);
  Comparator #(.width(32)) comparator_1 (.a(32'hc), .b(IR_q), .eq(comparator_1_eq));  // open: gt, lt
  or or_1 (or_1_out, \多周期硬布线控制器_1_pcwrite , and_1_out, and_2_out);
  RAM #(.addrWidth(10), .dataWidth(32), .bus("separate")) ram_1 (
    .addr(multiplexer_1_out[11:2]), .din(B_q), .data(ram_1_data), .str(\多周期硬布线控制器_1_memwrite ), .clk(CLK),
    .ld(\多周期硬布线控制器_1_memread ));  // open: sel, clr
  and and_1 (and_1_out, \多周期硬布线控制器_1_beq , mips_alu_1_equal);
  and and_2 (and_2_out, \多周期硬布线控制器_1_bne , ~mips_alu_1_equal);  // AND_Gate
  Register #(.width(32)) IR (.D(ram_1_data), .en(\多周期硬布线控制器_1_irwrite ), .Q(IR_q), .clk(CLK), .clr(RST));
  Register #(.width(32)) DR (.D(ram_1_data), .Q(DR_q), .clk(CLK), .clr(RST));  // open: en
  // Probe on \多周期硬布线控制器_1_当前状态 
  assign bit_extender_1_out = {{16{IR_q[15]}}, IR_q[15:0]};  // Bit_Extender bit_extender_1
  // Probe on \总周期数 
  \多周期硬布线控制器  \u_多周期硬布线控制器_1  (
    .RST(RST), .AluSrcB(\多周期硬布线控制器_1_alusrcb ), .OP(IR_q[31:26]), .CLK(CLK), .\当前状态 (\多周期硬布线控制器_1_当前状态 ),
    .IorD(\多周期硬布线控制器_1_iord ), .PCsrc(\多周期硬布线控制器_1_pcsrc ), .AluSrcA(\多周期硬布线控制器_1_alusrca ),
    .MemToReg(\多周期硬布线控制器_1_memtoreg ), .RegDst(\多周期硬布线控制器_1_regdst ), .IrWrite(\多周期硬布线控制器_1_irwrite ),
    .PcWrite(\多周期硬布线控制器_1_pcwrite ), .RegWrite(\多周期硬布线控制器_1_regwrite ), .MemWrite(\多周期硬布线控制器_1_memwrite ),
    .MemRead(\多周期硬布线控制器_1_memread ), .Beq(\多周期硬布线控制器_1_beq ), .Bne(\多周期硬布线控制器_1_bne ), .Func(IR_q[5:0]),
    .ALU_OP(\多周期硬布线控制器_1_alu_op ));
  Multiplexer #(.width(5), .enable("false")) multiplexer_2 (
    .in0(IR_q[20:16]), .in1(IR_q[15:11]), .out(multiplexer_2_out), .sel(\多周期硬布线控制器_1_regdst ));
  Multiplexer #(.width(32), .enable("false")) multiplexer_3 (
    .in0(C_q), .in1(DR_q), .out(multiplexer_3_out), .sel(\多周期硬布线控制器_1_memtoreg ));
  Shifter #(.width(32)) shifter_1 (.in(bit_extender_1_out), .\dist (5'b00010), .out(shifter_1_out));
  Register #(.width(32)) A (.D(mips_regifile_1_r1), .Q(A_q), .clk(CLK), .clr(RST));  // open: en
  MIPS_Regifile mips_regifile_1 (
    .Din(multiplexer_3_out), .Clk(CLK), .R1(mips_regifile_1_r1), .R2(mips_regifile_1_r2),
    .WE(\多周期硬布线控制器_1_regwrite ), .W_num(multiplexer_2_out), .R1_num(IR_q[25:21]), .R2_num(IR_q[20:16]));
  Register #(.width(32)) B (.D(mips_regifile_1_r2), .Q(B_q), .clk(CLK), .clr(RST));  // open: en
  Multiplexer #(.width(32), .enable("false")) multiplexer_4 (
    .in0(PC_q), .in1(A_q), .out(multiplexer_4_out), .sel(\多周期硬布线控制器_1_alusrca ));
  Multiplexer #(.select(2), .width(32), .enable("false")) multiplexer_5 (
    .in0(B_q), .in1(32'h4), .in2(bit_extender_1_out), .in3(shifter_1_out), .out(multiplexer_5_out),
    .sel(\多周期硬布线控制器_1_alusrcb ));
  MIPS_ALU mips_alu_1 (
    .X(multiplexer_4_out), .Y(multiplexer_5_out), .AluOP(\多周期硬布线控制器_1_alu_op ), .Equal(mips_alu_1_equal),
    .Result(mips_alu_1_result));  // open: Result_2
  Multiplexer #(.width(32), .enable("false")) multiplexer_6 (
    .in0(mips_alu_1_result), .in1(C_q), .out(multiplexer_6_out), .sel(\多周期硬布线控制器_1_pcsrc ));
  Register #(.width(32)) C (.D(mips_alu_1_result), .Q(C_q), .clk(CLK), .clr(RST));  // open: en

  // Notes on the sheet:
  //   存储器
  //   Ctrl+K  Command+K触发时钟连续仿真，程序运行结束后可停机，查看数据存储器中80单元的排序情况是有符号降序
  //   IorD
  //   MemWrite
  //   MemRead
  //   IRWrite
  //   OP
  //   Func
  //   RegDst
  //   PcWrite
  //   Beq
  //   Bne
  //   PcSrc
  //   AluOP
  //   AluSrcB
  //   AluSrcA
  //   RegWrite
  //   MemToReg
endmodule

// 硬布线控制器
module \多周期硬布线控制器  (
  input  [5:0] OP,
  input  [5:0] Func,
  input  CLK,
  input  RST,
  output [3:0] ALU_OP,
  output Bne,
  output Beq,
  output MemRead,
  output MemWrite,
  output RegWrite,
  output PcWrite,
  output IrWrite,
  output RegDst,
  output MemToReg,
  output [3:0] \当前状态 ,
  output [1:0] AluSrcB,
  output AluSrcA,
  output PCsrc,
  output IorD
);

  wire ADD, ADDI, BEQ_t, BNE_t, comparator_6_eq, comparator_9_eq, LW, or_1_out, P, R_TYPE, SLT, SW, SysCall;
  wire [1:0] ALU_Control;
  wire [3:0] and_3_out, and_4_out, or_2_out, rom_1_data, \状态机fsm_1_n0 ;
  wire [3:3] comparator_10_eq, comparator_11_eq;

  Comparator #(.width(6)) comparator_1 (.a(OP), .b(6'b100011), .eq(LW));  // open: gt, lt
  Comparator #(.width(6)) comparator_2 (.a(OP), .b(6'b101011), .eq(SW));  // open: gt, lt
  Comparator #(.width(6)) comparator_3 (.a(OP), .b(6'b000100), .eq(BEQ_t));  // open: gt, lt
  Comparator #(.width(6)) comparator_4 (.a(OP), .b(6'b000101), .eq(BNE_t));  // open: gt, lt
  Comparator #(.width(6)) comparator_5 (.a(OP), .b(6'b001000), .eq(ADDI));  // open: gt, lt
  Comparator #(.width(6)) comparator_6 (.a(OP), .b({6{1'b0}}), .eq(comparator_6_eq));  // open: gt, lt
  \状态机FSM  \u_状态机fsm_1  (
    .S3(\当前状态 [3]), .S2(\当前状态 [2]), .S1(\当前状态 [1]), .N3(\状态机fsm_1_n0 [3]), .S0(\当前状态 [0]), .R_Type(R_TYPE),
    .ADDI(ADDI), .LW(LW), .SW(SW), .BEQ(BEQ_t), .BNE(BNE_t), .SYSCALL(SysCall), .N2(\状态机fsm_1_n0 [2]),
    .N1(\状态机fsm_1_n0 [1]), .N0(\状态机fsm_1_n0 [0]));
  or or_1 (or_1_out, ADD, SLT);
  Comparator #(.width(6)) comparator_7 (.a(Func), .b(6'b100000), .eq(ADD));  // open: gt, lt
  Comparator #(.width(6)) comparator_8 (.a(Func), .b(6'b101010), .eq(SLT));  // open: gt, lt
  Comparator #(.width(6)) comparator_9 (.a(Func), .b(6'b001100), .eq(comparator_9_eq));  // open: gt, lt
  Register #(.width(4)) register_1 (.D(\状态机fsm_1_n0 ), .Q(\当前状态 ), .clk(CLK), .clr(RST));  // open: en
  and and_1 (R_TYPE, comparator_6_eq, or_1_out);
  and and_2 (SysCall, comparator_6_eq, comparator_9_eq);
  ROM #(.addrWidth(4), .dataWidth(21)) rom_1 (
    .addr(\当前状态 ),
    .data({IorD, PCsrc, AluSrcA, AluSrcB, MemToReg, RegDst, IrWrite, PcWrite, RegWrite, MemWrite, MemRead, Beq, Bne, ALU_Control, P, rom_1_data}));  // open: sel
  Comparator #(.width(6)) comparator_10 (.a(6'b101010), .b(Func), .eq(comparator_10_eq[3]));  // open: gt, lt
  Comparator #(.width(6)) comparator_11 (.a(Func), .b(6'b100000), .eq(comparator_11_eq[3]));  // open: gt, lt
  assign and_3_out = {4{comparator_10_eq[3]}} & 4'b1011;  // AND_Gate and_3, 4 bits wide
  assign or_2_out = and_3_out | and_4_out;  // OR_Gate or_2, 4 bits wide
  assign and_4_out = {4{comparator_11_eq[3]}} & 4'b0101;  // AND_Gate and_4, 4 bits wide
  Multiplexer #(.select(2), .width(4), .enable("false")) multiplexer_1 (
    .in0(4'b0101), .in1(4'b0110), .in2(or_2_out), .in3(4'b0101), .out(ALU_OP), .sel(ALU_Control));

  // Notes on the sheet:
  //   指令译码信号
  //   现态
  //   组合逻辑
  //   指令译码逻辑
  //   次态
  //   状态寄存器
  //   微程序控制器
  //   contents of rom_1 (hex, n*v repeats v):
  //   13201 30010 60003 130204 38800 60006 130400 40048 34800 c0100 c0080 6000c 30800 d
  //   ALU控制器逻辑
  //   根据ALU_Control的值决定运算器运算选择控制信号ALU_OP的值
  //   ALU_Control= 00 运算器做加法
  //   ALU_Control= 01 运算器做减法
  //   ALU_Control= 10 运算方式由Func决定 
endmodule

// 控制器状态机
module \状态机FSM  (
  input  S3,
  input  S2,
  input  S1,
  input  S0,
  input  R_Type,
  input  ADDI,
  input  LW,
  input  SW,
  input  BEQ,
  input  BNE,
  input  SYSCALL,
  output N3,
  output N2,
  output N1,
  output N0
);

  wire and_1_out, and_2_out, and_3_out, and_4_out, and_5_out, and_6_out, and_7_out, and_8_out, and_9_out,
       and_10_out, and_11_out, and_12_out, and_13_out, and_14_out, and_15_out, and_16_out, not_1_out,
       not_2_out, not_3_out, not_4_out, not_5_out, not_6_out, not_7_out, not_8_out, not_9_out, not_10_out,
       not_11_out, not_12_out, not_13_out, not_14_out, not_15_out, not_16_out, not_17_out, not_18_out,
       not_19_out, not_20_out, not_21_out, not_22_out, not_23_out, not_24_out, not_25_out, not_26_out,
       not_27_out, not_28_out, not_29_out, not_30_out, not_31_out, not_32_out, not_33_out, not_34_out,
       or_1_out, or_2_out, or_3_out, or_4_out;

  not not_1 (not_1_out, S3);
  not not_2 (not_2_out, S2);
  not not_3 (not_3_out, S1);
  not not_4 (not_4_out, S3);
  not not_5 (not_5_out, S2);
  not not_6 (not_6_out, S1);
  or or_1 (or_1_out, BNE, BEQ, ADDI, SYSCALL);
  not not_7 (not_7_out, S3);
  not not_8 (not_8_out, S2);
  not not_9 (not_9_out, S3);
  not not_10 (not_10_out, S1);
  not not_11 (not_11_out, S2);
  not not_12 (not_12_out, S1);
  not not_13 (not_13_out, S3);
  not not_14 (not_14_out, S2);
  not not_15 (not_15_out, S1);
  or or_2 (or_2_out, SW, R_Type, SYSCALL);
  not not_16 (not_16_out, S3);
  not not_17 (not_17_out, S2);
  not not_18 (not_18_out, S0);
  not not_19 (not_19_out, S3);
  not not_20 (not_20_out, S1);
  not not_21 (not_21_out, S3);
  not not_22 (not_22_out, S2);
  not not_23 (not_23_out, S1);
  or or_3 (or_3_out, LW, R_Type, BNE, ADDI);
  not not_24 (not_24_out, S3);
  not not_25 (not_25_out, S2);
  not not_26 (not_26_out, S1);
  not not_27 (not_27_out, S0);
  not not_28 (not_28_out, S3);
  not not_29 (not_29_out, S2);
  not not_30 (not_30_out, S0);
  not not_31 (not_31_out, S1);
  not not_32 (not_32_out, S3);
  not not_33 (not_33_out, S2);
  not not_34 (not_34_out, S1);
  or or_4 (or_4_out, SW, R_Type, BEQ, ADDI, SYSCALL);
  and and_1 (and_1_out, not_1_out, S2, S1, S0);
  and and_2 (and_2_out, S3, not_2_out, S1, S0);
  and and_3 (and_3_out, S3, S2, not_3_out, S0);
  and and_4 (and_4_out, not_4_out, not_5_out, not_6_out, S0, or_1_out);
  and and_5 (and_5_out, not_7_out, not_8_out, S1, S0);
  and and_6 (and_6_out, not_9_out, S2, not_10_out, S0);
  and and_7 (and_7_out, S3, not_11_out, S1, S0);
  and and_8 (and_8_out, S3, S2, not_12_out, S0);
  and and_9 (and_9_out, not_13_out, not_14_out, not_15_out, S0, or_2_out);
  and and_10 (and_10_out, not_16_out, not_17_out, S1, not_18_out);
  and and_11 (and_11_out, not_19_out, S2, not_20_out, S0);
  and and_12 (and_12_out, not_21_out, not_22_out, not_23_out, S0, or_3_out);
  and and_13 (and_13_out, not_24_out, not_25_out, not_26_out, not_27_out);
  and and_14 (and_14_out, not_28_out, not_29_out, S1, not_30_out);
  and and_15 (and_15_out, S3, S2, not_31_out, S0);
  and and_16 (and_16_out, not_32_out, not_33_out, not_34_out, S0, or_4_out);
  or or_5 (N3, and_1_out, and_2_out, and_3_out, and_4_out);
  or or_6 (N2, and_5_out, and_6_out, and_7_out, and_8_out, and_9_out);
  or or_7 (N1, and_10_out, and_11_out, and_12_out);
  or or_8 (N0, and_13_out, and_14_out, and_15_out, and_16_out);
endmodule

module MIPS_Regifile (
  input  [31:0] Din,
  input  Clk,
  input  WE,
  input  [4:0] R1_num,
  input  [4:0] W_num,
  input  [4:0] R2_num,
  output [31:0] R1,
  output [31:0] R2
);

  // RegisterFile registerfile_1: pin names not known; wires that end beside it: Din, Clk, WE, W_num, R1_num, R2_num, R1, R2
endmodule

// ALU
module MIPS_ALU (
  input  [31:0] X,
  input  [31:0] Y,
  input  [3:0] AluOP,
  output Equal,
  output [31:0] Result,
  output [31:0] Result_2
);

  wire [0:0] comparator_1_lt, comparator_2_lt;
  wire [31:0] adder_1_out, AND_out, divider_1_out, divider_1_rem, multiplier_1_cout, multiplier_1_out,
       NOR_out, OR_out, shifter_1_out, shifter_2_out, shifter_3_out, subtractor_1_out, XOR_out;

  Shifter #(.width(32)) shifter_1 (.in(X), .\dist (Y[4:0]), .out(shifter_1_out));
  Shifter #(.width(32), .shift("ar")) shifter_2 (.in(X), .\dist (Y[4:0]), .out(shifter_2_out));
  Shifter #(.width(32), .shift("lr")) shifter_3 (.in(X), .\dist (Y[4:0]), .out(shifter_3_out));
  Multiplier #(.width(32)) multiplier_1 (.a(X), .b(Y), .out(multiplier_1_out), .cout(multiplier_1_cout));  // open: cin
  Divider #(.width(32)) divider_1 (.a(X), .b(Y), .out(divider_1_out), .rem(divider_1_rem));  // open: upper
  Adder #(.width(32)) adder_1 (.a(X), .b(Y), .out(adder_1_out));  // open: cin, cout
  Subtractor #(.width(32)) subtractor_1 (.a(X), .b(Y), .out(subtractor_1_out));  // open: bin, bout
  assign AND_out = X & Y;  // AND_Gate AND, 32 bits wide
  assign OR_out = X | Y;  // OR_Gate OR, 32 bits wide
  assign XOR_out = X ^ Y;  // XOR_Gate XOR, 32 bits wide
  assign NOR_out = ~(X | Y);  // NOR_Gate NOR, 32 bits wide
  Comparator #(.width(32)) comparator_1 (.a(X), .b(Y), .eq(Equal), .lt(comparator_1_lt[0]));  // open: gt
  Comparator #(.width(32)) comparator_2 (.a(X), .b(Y), .lt(comparator_2_lt[0]));  // open: gt, eq
  Multiplexer #(.select(4), .width(32), .enable("false")) multiplexer_1 (
    .in0(shifter_1_out), .in1(shifter_2_out), .in2(shifter_3_out), .in3(multiplier_1_out),
    .in4(divider_1_out), .in5(adder_1_out), .in6(subtractor_1_out), .in7(AND_out), .in8(OR_out),
    .in9(XOR_out), .in10(NOR_out), .in11({{31{1'b0}}, comparator_1_lt[0]}),
    .in12({{31{1'b0}}, comparator_2_lt[0]}), .in13({32{1'b0}}), .in14({32{1'b0}}), .in15({32{1'b0}}),
    .out(Result), .sel(AluOP));
  Multiplexer #(.select(4), .width(32), .enable("false")) multiplexer_2 (
    .in0({32{1'b0}}), .in1({32{1'b0}}), .in2({32{1'b0}}), .in3(multiplier_1_cout), .in4(divider_1_rem),
    .in5({32{1'b0}}), .in6({32{1'b0}}), .in7({32{1'b0}}), .in8({32{1'b0}}), .in9({32{1'b0}}),
    .in10({32{1'b0}}), .in11({32{1'b0}}), .in12({32{1'b0}}), .in13({32{1'b0}}), .in14({32{1'b0}}),
    .in15({32{1'b0}}), .out(Result_2), .sel(AluOP));

  // Other names for the same wires on the sheet: Result2[31:0] = Result_2; S[3:0] = AluOP

  // Notes on the sheet:
  //   不要改变此引脚区域内容，也不要改变ALU封装形式
  //   输入引脚
  //   输出引脚
endmodule
